# Fritzing sketch CharliePlexing (saved by Fritzing 0.8.7b)
breadboards: 1

parts:
  U1 = atmega328 [package=dip]
  R1 = Resistor [tolerance=±5% resistance=10k package=THT]
  C1 = Ceramic Capacitor [capacitance=100nF package="100 mil [THT, multilayer]"]
  LED1 = LED - 5mm [color="Red (633nm)" package="5 mm [THT]"]
  LED3 = LED - 5mm [color="Red (633nm)" package="5 mm [THT]"]
  LED4 = LED - 5mm [color="Red (633nm)" package="5 mm [THT]"]
  LED5 = LED - 5mm [color="Red (633nm)" package="5 mm [THT]"]
  LED6 = LED - 5mm [color="Red (633nm)" package="5 mm [THT]"]
  LED2 = LED - 5mm [color="Red (633nm)" package="5 mm [THT]"]

nets:
  N1: U1.RESET, R1.Pin_0, C1.1
  N2: U1.VCC, R1.Pin_1
  N3: U1.D6_(PWM), LED1.cathode, LED3.cathode, LED4.anode, LED2.anode
  N4: U1.D7, LED1.anode, LED5.cathode, LED6.anode, LED2.cathode
  N5: U1.D8, LED3.anode, LED4.cathode, LED5.anode, LED6.cathode
