# Fritzing sketch Klaviatuur (saved by Fritzing 0.8.7b)
breadboards: 1

parts:
  U1 = atmega328 [package=dip]
  R1 = Resistor [tolerance=±5% resistance=10k package=THT]
  C1 = Ceramic Capacitor [capacitance=100nF package="100 mil [THT, multilayer]"]
  JP1 = Header 8 [package=1x08_smd_alt]

nets:
  N1: U1.RESET, R1.Pin_0, C1.1
  N2: U1.D3_(PWM), JP1.1
  N3: U1.D4, JP1.2
  N4: U1.VCC, R1.Pin_1
  N5: U1.XLAT1, JP1.3
  N6: U1.XLAT2, JP1.4
  N7: U1.D5_(PWM), JP1.5
  N8: U1.D6_(PWM), JP1.6
  N9: U1.D7, JP1.7
  N10: U1.D8, JP1.8
