# Fritzing sketch PatareiPinge2 (saved by Fritzing 0.8.7b)
breadboards: 1

parts:
  U1 = atmega328 [package=dip]
  R1 = Resistor [tolerance=±5% resistance=10k package=THT]
  C1 = Ceramic Capacitor [capacitance=100nF package="100 mil [THT, multilayer]"]
  R2 = Resistor [tolerance=±5% resistance=3.3 package=THT]
  R3 = Resistor [tolerance=±5% resistance=3.3 package=THT]
  R4 = Resistor [tolerance=±5% resistance=3.3 package=THT]

nets:
  N1: U1.RESET, R1.Pin_0, C1.1
  N2: U1.D4, R3.Pin_1
  N3: U1.VCC, U1.AVCC, R1.Pin_1
  N4: U1.GND, R2.Pin_1
  N5: U1.A5, R2.Pin_0, R4.Pin_0
  N6: R3.Pin_0, R4.Pin_1
