# Fritzing sketch Vilgutaja (saved by Fritzing 0.8.7b)
breadboards: 1

parts:
  U1 = atmega328 [package=dip]
  R1 = Resistor [tolerance=±5% resistance=10k package=THT]
  C1 = Ceramic Capacitor [capacitance=100nF package="100 mil [THT, multilayer]"]
  LED1 = smd LED [color="Red (633nm)" package="0603 [SMD]"]
  LED2 = smd LED [color="Blue (525nm)" package="0603 [SMD]"]

nets:
  N1: U1.RESET, R1.Pin_0, C1.1
  N2: U1.VCC, R1.Pin_1
  N3: U1.D7, LED1.cathode, LED2.anode
  N4: U1.D8, LED1.anode, LED2.cathode
